# Fritzing sketch Circuit Structure Diagram (saved by Fritzing 0.9.3b)
breadboards: 1

parts:
  부품1 = Arduino Uno (Rev3)
  부품3 = Thumb Joystick
  LCD1 = LCD screen  # not connected
  부품4 = Breakout Board for Electret Microphone
  hc-sr1 = hc-sr04
  LED1 = LED - 5mm [color="Red (633nm)" package="5 mm [THT]"]
  LED2 = LED - 5mm [color="Red (633nm)" package="5 mm [THT]"]
  LED3 = LED - 5mm [color="Red (633nm)" package="5 mm [THT]"]
  LED4 = LED - 5mm [color="Red (633nm)" package="5 mm [THT]"]
  R1 = Rotary Potentiometer (Small) [maximum_resistance=100kΩ package=THT]
  R2 = Resistor [tolerance=±5% resistance=220 package="0603 [SMD]"]
  R3 = Resistor [tolerance=±5% resistance=220 package="0603 [SMD]"]
  R4 = Resistor [tolerance=±5% resistance=220 package="0603 [SMD]"]
  R5 = Resistor [tolerance=±5% resistance=220 package="0603 [SMD]"]
  RHT1 = Humidity and Temperature Sensor RHT03
  부품5 = Bluetooth HC-05 Macho
  J1 = Piezo Speaker
  IC1 = L293D [package=THT]
  M1 = DC Motor
  J2 = Basic Servo

nets:
  N1: 부품1.A0, R1.wiper
  N2: 부품1.A1, 부품4.VCC
  N3: 부품1.A2, 부품3.SEL
  N4: 부품1.A3, 부품3.HORZ
  N5: 부품1.D9_PWM, R2.Pin_1
  N6: 부품1.D10_PWM/SS, R3.Pin_1
  N7: 부품1.D11_PWM/MOSI, R4.Pin_1
  N8: 부품1.D12/MISO, R5.Pin_1
  N9: 부품1.D13/SCK, RHT1.Data-signal
  N10: 부품1.D0/RX, 부품5.RXD
  N11: 부품1.D1/TX, 부품5.TXD
  N12: 부품1.D2, J1.pin2
  N13: 부품1.D3_PWM, hc-sr1.Trig
  N14: 부품1.D4, hc-sr1.Echo
  N15: 부품1.D5_PWM, IC1.In_4
  N16: 부품1.D6_PWM, IC1.In_3
  N17: 부품1.D7, IC1.Enable_2
  VCC: 부품1.5V, 부품3.VCC, 부품4.AUD, hc-sr1.VCC, R1.leg1, RHT1.Vcc, 부품5.VCC, IC1.+Vmotor, IC1.+V, J2.vcc
  GND: 부품1.GND, 부품3.VERT, 부품4.GND, hc-sr1.GND, LED1.cathode, LED2.cathode, LED3.cathode, LED4.cathode, R1.leg2, RHT1.GND_2, 부품5.GND, J1.pin1, IC1.0V, J2.gnd
  N18: LED1.anode, R5.Pin_0
  N19: LED2.anode, R4.Pin_0
  N20: LED3.anode, R3.Pin_0
  N21: LED4.anode, R2.Pin_0
  N22: IC1.Out_3_(_Controlled_by_Enable_2_), M1.pin_2
  N23: IC1.Out_4_(_Controlled_by_Enable_2_), M1.pin_1
